# Fritzing sketch isCold (saved by Fritzing 0.9.3b)
breadboards: 1

parts:
  Breakout1 = BMP280 [package=Breakout]
  Raspberry_Pi1 = Raspberry Pi B+
  R1 = Resistor [tolerance=±5% resistance=220 package=THT]
  LED1 = smd LED [color="Red (633nm)" package="1206 [SMD]"]

nets:
  VIN: Breakout1.VIN, Raspberry_Pi1.5V
  GND: Breakout1.GND, Raspberry_Pi1.GND, LED1.cathode
  N1: Breakout1.SCK, Raspberry_Pi1.GPIO3
  N2: Breakout1.SDI, Raspberry_Pi1.GPIO2
  N3: Raspberry_Pi1.GIPO4, R1.Pin_1
  N4: R1.Pin_0, LED1.anode

custom parts:
  BMP280: Barometric Pressure and Temperature Sensor
  Raspberry Pi B+: The awesome Raspberry Pi ARM Board with 40 pin gipo. Ready for special designed Raspberry Pi B+ Hat (Hardware attached (on) top)
